# Fritzing sketch wiring_diagram (saved by Fritzing 0.9.0b)

parts:
  TRINKET1 = Trinket 3V
  FLORA1 = Flora Accelerometer/Compass Sensor
  MIC1 = MAX9814 Electret Microphone Breakout Board
  BATT2 = LiPoly Battery (110mAh)  # not connected
  J1 = male pin header, 2 pins [form="♂ (male)"]
  NEOPIXEL1 = Neopixel Strip -- Black (60/m)

nets:
  N1: TRINKET1.no_name_yet#1, J1.pin1
  N2: TRINKET1.no_name_yet#3, MIC1.out
  N3: TRINKET1.no_name_yet#7, FLORA1.SCL
  N4: TRINKET1.no_name_yet#8, NEOPIXEL1.DI
  N5: TRINKET1.no_name_yet#9, FLORA1.SDA

custom parts:
  Trinket 3V: Adafruit Trinket 3V
  Flora Accelerometer/Compass Sensor: Flora Accelerometer and Compass Sensor - LSM303
  MAX9814 Electret Microphone Breakout Board: MAX9814 Electrec Microphone Breakout Board
  LiPoly Battery (110mAh): Lithium Ion Polymer Battery (110mAh)
  Neopixel Strip -- Black (60/m): Neopixel Strip, Black, 60 pixels per meter.
